# Fritzing sketch All (saved by Fritzing 0.9.4)
breadboards: 2

parts:
  パーツ1 = Arduino Nano (Rev3.0)
  Power_plug1 = Power plug
  IC3 = IC, DIP package, 18 pins [chip_label=IC]
  IC4 = IC, DIP package, 10 pins [chip_label=IC]
  J1 = Basic Servo
  R3 = Photocell (LDR) [package=THT]
  R4 = Resistor [tolerance=±5% resistance=1k package=THT]
  IC5 = IC, DIP package, 16 pins [chip_label=IC]

nets:
  GND: パーツ1.GND, Power_plug1.GND, IC3.pin13, IC4.pin8, IC4.pin9, J1.gnd, R4.Pin_1, IC5.pin5
  N1: パーツ1.D4, J1.pulse
  N2: パーツ1.D7, IC5.pin1
  N3: パーツ1.D8, IC4.pin7
  N4: パーツ1.D10, IC3.pin17
  N5: パーツ1.D11/MOSI, IC3.pin16, IC5.pin2
  N6: パーツ1.D12/MISO, IC3.pin15, IC5.pin3
  VIN: パーツ1.VIN, Power_plug1.VCC
  5V: パーツ1.5V, IC3.pin10, IC4.pin10, J1.vcc, R3.pin_0, IC5.pin6
  N7: パーツ1.A5, IC5.pin8
  N8: パーツ1.A4, IC5.pin7
  N9: パーツ1.A1, R3.pin_1, R4.Pin_0
  N10: パーツ1.D13/SCK, IC3.pin14, IC5.pin4

notes:
  12V
  5V
  3.3V
  SD
  Camera
  GPS
  Servo
  Light
  Barometer
  IMU
  1kΩ
