# Fritzing sketch DCMotor_x2 (saved by Fritzing 0.9.3b)
breadboards: 1

parts:
  パーツ1 = Arduino Nano (Rev3.0)
  Power_plug1 = Power plug
  C2 = Ceramic Capacitor [capacitance=100nF package="100 mil [THT, multilayer]"]
  C3 = Electrolytic Capacitor [capacitance=1µF package="100 mil [THT, electrolytic]"]
  VCC1 = Battery
  C4 = Ceramic Capacitor [capacitance=100nF package="100 mil [THT, multilayer]"]
  C6 = Ceramic Capacitor [capacitance=100nF package="100 mil [THT, multilayer]"]
  M3 = DC Motor
  M4 = DC Motor

nets:
  GND: パーツ1.GND, Power_plug1.GND, C2.0, C3.-, VCC1.-
  VIN: パーツ1.VIN, Power_plug1.VCC
  N1: C2.1, C3.+, VCC1.+
  N2: C4.0, M3.pin_2
  N3: C4.1, M3.pin_1
  N4: C6.0, M4.pin_2
  N5: C6.1, M4.pin_1

notes:
  12V
  5V
  100uF
  0.1uF
  MotorDriver
  DC Motor
  Battery for DC motor
